// Logisim project LamNgoFinalProject.circ as structural Verilog: 9 circuits, main circuit 16-bit carry look ahead
module _16_bit_carry_look_ahead (
  input  [15:0] A,
  input  [15:0] B,
  input  c_in,
  output Cout,
  output [15:0] out_5
);

  wire n4_bit_carry_look_ahead_adder_2_cout, n4_bit_carry_look_ahead_adder_3_cout,
       n4_bit_carry_look_ahead_adder_4_cout;

  _4_bit_Carry_Look_Ahead_adder u_4_bit_carry_look_ahead_adder_1 (
    .Cin(n4_bit_carry_look_ahead_adder_2_cout), .A(A[15:12]), .B(B[15:12]), .Out(out_5[15:12]), .Cout(Cout));
  _4_bit_Carry_Look_Ahead_adder u_4_bit_carry_look_ahead_adder_2 (
    .Cin(n4_bit_carry_look_ahead_adder_3_cout), .A(A[11:8]), .B(B[11:8]), .Out(out_5[11:8]),
    .Cout(n4_bit_carry_look_ahead_adder_2_cout));
  _4_bit_Carry_Look_Ahead_adder u_4_bit_carry_look_ahead_adder_3 (
    .Cin(n4_bit_carry_look_ahead_adder_4_cout), .A(A[7:4]), .B(B[7:4]), .Out(out_5[7:4]),
    .Cout(n4_bit_carry_look_ahead_adder_3_cout));
  _4_bit_Carry_Look_Ahead_adder u_4_bit_carry_look_ahead_adder_4 (
    .Cin(c_in), .A(A[3:0]), .B(B[3:0]), .Out(out_5[3:0]), .Cout(n4_bit_carry_look_ahead_adder_4_cout));
endmodule

module _4_bit_Carry_Look_Ahead_adder (
  input  Cin,
  input  [3:0] A,
  input  [3:0] B,
  output [3:0] Out,
  output Cout
);

  wire and_1_out, and_2_out, and_3_out, and_4_out, and_5_out, n1_bit_adder_1_g, n1_bit_adder_1_p,
       n1_bit_adder_2_cout, n1_bit_adder_2_g, n1_bit_adder_2_p, n1_bit_adder_3_cout, n1_bit_adder_3_g,
       n1_bit_adder_3_p, n1_bit_adder_4_cout, n1_bit_adder_4_g, n1_bit_adder_4_p, or_1_out, or_2_out,
       or_3_out;

  _1_bit_adder u_1_bit_adder_1 (
    .A(A[3]), .B(B[3]), .Cin(n1_bit_adder_2_cout), .Sum(Out[3]), .G(n1_bit_adder_1_g), .P(n1_bit_adder_1_p));  // open: Cout
  _1_bit_adder u_1_bit_adder_2 (
    .A(A[2]), .B(B[2]), .Cin(n1_bit_adder_3_cout), .Sum(Out[2]), .Cout(n1_bit_adder_2_cout),
    .G(n1_bit_adder_2_g), .P(n1_bit_adder_2_p));
  _1_bit_adder u_1_bit_adder_3 (
    .A(A[1]), .B(B[1]), .Cin(n1_bit_adder_4_cout), .Sum(Out[1]), .Cout(n1_bit_adder_3_cout),
    .G(n1_bit_adder_3_g), .P(n1_bit_adder_3_p));
  _1_bit_adder u_1_bit_adder_4 (
    .A(A[0]), .B(B[0]), .Cin(Cin), .Sum(Out[0]), .Cout(n1_bit_adder_4_cout), .G(n1_bit_adder_4_g),
    .P(n1_bit_adder_4_p));
  and and_1 (and_1_out, n1_bit_adder_3_p, n1_bit_adder_4_g);
  or or_1 (or_1_out, n1_bit_adder_3_g, and_1_out);
  and and_2 (and_2_out, n1_bit_adder_1_p, n1_bit_adder_2_p, n1_bit_adder_3_p, n1_bit_adder_4_p);
  or or_2 (or_2_out, n1_bit_adder_2_g, and_3_out);
  and and_3 (and_3_out, n1_bit_adder_2_p, or_1_out);
  or or_3 (or_3_out, n1_bit_adder_1_g, and_4_out);
  and and_4 (and_4_out, n1_bit_adder_1_p, or_2_out);
  and and_5 (and_5_out, and_2_out, Cin);
  or or_4 (Cout, or_3_out, and_5_out);
endmodule

module _1_bit_adder (
  input  A,
  input  B,
  input  Cin,
  output Sum,
  output Cout,
  output G,
  output P
);

  wire and_2_out, xor_1_out;

  xor xor_1 (xor_1_out, A, B);
  and and_1 (G, B, A);
  xor xor_2 (Sum, xor_1_out, Cin);
  and and_2 (and_2_out, Cin, xor_1_out);
  or or_1 (P, B, A);
  or or_2 (Cout, and_2_out, G);
endmodule

module Control_Signal (
  input  [8:0] in_1,
  output Intermediate,
  output RegWrite,
  output load,
  output store,
  output Branch,
  output Jump,
  output [2:0] ALU,
  output Data_memory_Select
);

  or or_1 (Data_memory_Select, in_1[5], in_1[6]);

  assign ALU = in_1[2:0];
  assign Branch = in_1[4];
  assign Intermediate = in_1[8];
  assign Jump = in_1[3];
  assign load = in_1[6];
  assign RegWrite = in_1[7];
  assign store = in_1[5];
endmodule

module Basic_CPU (
  input  Clock
);

  wire control_signal_1_data_memory_select, control_signal_1_intermediate, control_signal_1_load,
       control_signal_1_regwrite, control_signal_1_store;
  wire [2:0] control_signal_1_alu;
  wire [3:0] multiplexer_1_out;
  wire [15:0] bit_extender_1_out, multiplexer_2_out, multiplexer_3_out, n16_bit_alu_1_out_5,
       n16_bit_carry_look_ahead_1_out_5, ram_2_data, regfile_1_read_1_data, regfile_1_read_2_data,
       register_1_q;
  wire [20:0] ram_1_data;

  Register #(.width(16)) register_1 (
    .D(n16_bit_carry_look_ahead_1_out_5), .Q(register_1_q), .clk(Clock));  // open: en, clr
  _16_bit_carry_look_ahead u_16_bit_carry_look_ahead_1 (
    .A(16'h1), .B(register_1_q), .c_in(1'b0), .out_5(n16_bit_carry_look_ahead_1_out_5));  // open: Cout
  RAM #(.addrWidth(16), .dataWidth(21)) ram_1 (
    .addr(register_1_q), .data(ram_1_data), .clk(Clock));  // open: sel, ld, clr
  Control_Signal control_signal_1 (
    .in_1(ram_1_data[20:12]), .Intermediate(control_signal_1_intermediate),
    .RegWrite(control_signal_1_regwrite), .load(control_signal_1_load), .store(control_signal_1_store),
    .ALU(control_signal_1_alu), .Data_memory_Select(control_signal_1_data_memory_select));  // open: Branch, Jump
  Multiplexer #(.width(4), .enable("false")) multiplexer_1 (
    .in0(ram_1_data[3:0]), .in1(ram_1_data[11:8]), .out(multiplexer_1_out), .sel(control_signal_1_store));
  REGFILE regfile_1 (
    .data_in(multiplexer_3_out), .Clock(Clock), .Write_Enable(control_signal_1_regwrite),
    .Write_Addr(ram_1_data[11:8]), .Read_Addr_1(ram_1_data[7:4]), .Read_Addr_2(multiplexer_1_out),
    .Read_1_Data(regfile_1_read_1_data), .Read_2_Data(regfile_1_read_2_data));
  assign bit_extender_1_out = {{12{ram_1_data[3]}}, ram_1_data[3:0]};  // Bit_Extender bit_extender_1
  Multiplexer #(.width(16), .enable("false")) multiplexer_2 (
    .in0(regfile_1_read_2_data), .in1(bit_extender_1_out), .out(multiplexer_2_out),
    .sel(control_signal_1_intermediate));
  Multiplexer #(.width(16), .enable("false")) multiplexer_3 (
    .in0(n16_bit_alu_1_out_5), .in1(ram_2_data), .out(multiplexer_3_out), .sel(control_signal_1_load));
  _16_bit_ALU u_16_bit_alu_1 (
    .A(regfile_1_read_1_data), .B(multiplexer_2_out), .in_3(control_signal_1_alu), .out_5(n16_bit_alu_1_out_5));  // open: Zero_Flag
  RAM #(.addrWidth(16), .dataWidth(16), .bus("separate")) ram_2 (
    .addr(n16_bit_alu_1_out_5), .din(regfile_1_read_2_data), .data(ram_2_data), .str(control_signal_1_store),
    .sel(control_signal_1_data_memory_select), .clk(Clock), .ld(control_signal_1_load));  // open: clr
endmodule

module REGFILE (
  input  [15:0] data_in,
  input  [3:0] Read_Addr_1,
  input  Write_Enable,
  input  [3:0] Write_Addr,
  input  [3:0] Read_Addr_2,
  input  Clock,
  output [15:0] Read_1_Data,
  output [15:0] Read_2_Data
);

  wire demultiplexer_1_out0, demultiplexer_1_out1, demultiplexer_1_out2, demultiplexer_1_out3,
       demultiplexer_1_out4, demultiplexer_1_out5, demultiplexer_1_out6, demultiplexer_1_out7,
       demultiplexer_1_out8, demultiplexer_1_out9, demultiplexer_1_out10, demultiplexer_1_out11,
       demultiplexer_1_out12, demultiplexer_1_out13, demultiplexer_1_out14, demultiplexer_1_out15;
  wire [15:0] _0_q, _1_q, _2_q, _3_q, _4_q, _5_q, _6_q, _7_q, _8_q, a0_q, a1_q, at_q, ra_q, sp_q, v0_q, v1_q;

  Demultiplexer #(.select(4), .enable("false")) demultiplexer_1 (
    .out0(demultiplexer_1_out0), .out1(demultiplexer_1_out1), .out2(demultiplexer_1_out2),
    .out3(demultiplexer_1_out3), .out4(demultiplexer_1_out4), .out5(demultiplexer_1_out5),
    .out6(demultiplexer_1_out6), .out7(demultiplexer_1_out7), .out8(demultiplexer_1_out8),
    .out9(demultiplexer_1_out9), .out10(demultiplexer_1_out10), .out11(demultiplexer_1_out11),
    .out12(demultiplexer_1_out12), .out13(demultiplexer_1_out13), .out14(demultiplexer_1_out14),
    .out15(demultiplexer_1_out15), .in(Write_Enable), .sel(Write_Addr));
  Register #(.width(16)) _0 (.D(data_in), .en(demultiplexer_1_out0), .Q(_0_q), .clk(Clock));  // open: clr
  Register #(.width(16)) _1 (.D(data_in), .en(demultiplexer_1_out1), .Q(_1_q), .clk(Clock));  // open: clr
  Register #(.width(16)) _2 (.D(data_in), .en(demultiplexer_1_out2), .Q(_2_q), .clk(Clock));  // open: clr
  Register #(.width(16)) _3 (.D(data_in), .en(demultiplexer_1_out3), .Q(_3_q), .clk(Clock));  // open: clr
  Register #(.width(16)) _4 (.D(data_in), .en(demultiplexer_1_out4), .Q(_4_q), .clk(Clock));  // open: clr
  Register #(.width(16)) _5 (.D(data_in), .en(demultiplexer_1_out5), .Q(_5_q), .clk(Clock));  // open: clr
  Register #(.width(16)) _6 (.D(data_in), .en(demultiplexer_1_out6), .Q(_6_q), .clk(Clock));  // open: clr
  Register #(.width(16)) _7 (.D(data_in), .en(demultiplexer_1_out7), .Q(_7_q), .clk(Clock));  // open: clr
  Register #(.width(16)) _8 (.D(data_in), .en(demultiplexer_1_out8), .Q(_8_q), .clk(Clock));  // open: clr
  Register #(.width(16)) v1 (.D(data_in), .en(demultiplexer_1_out9), .Q(v1_q), .clk(Clock));  // open: clr
  Register #(.width(16)) v0 (.D(data_in), .en(demultiplexer_1_out10), .Q(v0_q), .clk(Clock));  // open: clr
  Register #(.width(16)) a1 (.D(data_in), .en(demultiplexer_1_out11), .Q(a1_q), .clk(Clock));  // open: clr
  Register #(.width(16)) a0 (.D(data_in), .en(demultiplexer_1_out12), .Q(a0_q), .clk(Clock));  // open: clr
  Register #(.width(16)) at (.D(data_in), .en(demultiplexer_1_out13), .Q(at_q), .clk(Clock));  // open: clr
  Register #(.width(16)) ra (.D(data_in), .en(demultiplexer_1_out14), .Q(ra_q), .clk(Clock));  // open: clr
  Register #(.width(16)) sp (.D(data_in), .en(demultiplexer_1_out15), .Q(sp_q), .clk(Clock));  // open: clr
  Multiplexer #(.select(4), .width(16), .enable("false")) multiplexer_1 (
    .in0(_0_q), .in1(_1_q), .in2(_2_q), .in3(_3_q), .in4(_4_q), .in5(_5_q), .in6(_6_q), .in7(_7_q),
    .in8(_8_q), .in9(v1_q), .in10(v0_q), .in11(a1_q), .in12(a0_q), .in13(at_q), .in14(ra_q), .in15(sp_q),
    .out(Read_1_Data), .sel(Read_Addr_1));
  Multiplexer #(.select(4), .width(16), .enable("false")) multiplexer_2 (
    .in0(_0_q), .in1(_1_q), .in2(_2_q), .in3(_3_q), .in4(_4_q), .in5(_5_q), .in6(_6_q), .in7(_7_q),
    .in8(_8_q), .in9(v1_q), .in10(v0_q), .in11(a1_q), .in12(a0_q), .in13(at_q), .in14(ra_q), .in15(sp_q),
    .out(Read_2_Data), .sel(Read_Addr_2));
endmodule

module CPU_with_Branch (
  input  Clock
);

  wire and_1_out, control_signal_1_branch, control_signal_1_data_memory_select,
       control_signal_1_intermediate, control_signal_1_load, control_signal_1_regwrite,
       control_signal_1_store, n16_bit_alu_1_zero_flag, or_1_out;
  wire [2:0] control_signal_1_alu;
  wire [3:0] multiplexer_2_out, ram_1_data;
  wire [15:0] bit_extender_1_out, bit_extender_2_out, multiplexer_1_out, multiplexer_3_out,
       multiplexer_4_out, n16_bit_alu_1_out_5, n16_bit_carry_look_ahead_1_out_5,
       n16_bit_carry_look_ahead_2_out_5, ram_2_data, regfile_1_read_1_data, regfile_1_read_2_data,
       register_1_q;
  wire [20:4] ram_1_data_2;

  assign bit_extender_1_out = {{12{ram_1_data[3]}}, ram_1_data};  // Bit_Extender bit_extender_1
  Multiplexer #(.width(16), .enable("false")) multiplexer_1 (
    .in0(n16_bit_carry_look_ahead_2_out_5), .in1(n16_bit_carry_look_ahead_1_out_5), .out(multiplexer_1_out),
    .sel(and_1_out));
  _16_bit_carry_look_ahead u_16_bit_carry_look_ahead_1 (
    .A(n16_bit_carry_look_ahead_2_out_5), .B(bit_extender_1_out), .c_in(1'b0),
    .out_5(n16_bit_carry_look_ahead_1_out_5));  // open: Cout
  Register #(.width(16)) register_1 (.D(multiplexer_1_out), .Q(register_1_q), .clk(Clock));  // open: en, clr
  _16_bit_carry_look_ahead u_16_bit_carry_look_ahead_2 (
    .A(16'h1), .B(register_1_q), .c_in(1'b0), .out_5(n16_bit_carry_look_ahead_2_out_5));  // open: Cout
  RAM #(.addrWidth(16), .dataWidth(21)) ram_1 (
    .addr(register_1_q), .data({ram_1_data_2, ram_1_data}), .clk(Clock));  // open: sel, ld, clr
  Control_Signal control_signal_1 (
    .in_1(ram_1_data_2[20:12]), .Intermediate(control_signal_1_intermediate),
    .RegWrite(control_signal_1_regwrite), .load(control_signal_1_load), .store(control_signal_1_store),
    .Branch(control_signal_1_branch), .ALU(control_signal_1_alu),
    .Data_memory_Select(control_signal_1_data_memory_select));  // open: Jump
  or or_1 (or_1_out, control_signal_1_branch, control_signal_1_store);
  Multiplexer #(.width(4), .enable("false")) multiplexer_2 (
    .in0(ram_1_data), .in1(ram_1_data_2[11:8]), .out(multiplexer_2_out), .sel(or_1_out));
  REGFILE regfile_1 (
    .data_in(multiplexer_4_out), .Clock(Clock), .Write_Enable(control_signal_1_regwrite),
    .Write_Addr(ram_1_data_2[11:8]), .Read_Addr_1(ram_1_data_2[7:4]), .Read_Addr_2(multiplexer_2_out),
    .Read_1_Data(regfile_1_read_1_data), .Read_2_Data(regfile_1_read_2_data));
  assign bit_extender_2_out = {{12{ram_1_data[3]}}, ram_1_data};  // Bit_Extender bit_extender_2
  Multiplexer #(.width(16), .enable("false")) multiplexer_3 (
    .in0(regfile_1_read_2_data), .in1(bit_extender_2_out), .out(multiplexer_3_out),
    .sel(control_signal_1_intermediate));
  Multiplexer #(.width(16), .enable("false")) multiplexer_4 (
    .in0(n16_bit_alu_1_out_5), .in1(ram_2_data), .out(multiplexer_4_out), .sel(control_signal_1_load));
  _16_bit_ALU u_16_bit_alu_1 (
    .A(regfile_1_read_1_data), .B(multiplexer_3_out), .in_3(control_signal_1_alu),
    .Zero_Flag(n16_bit_alu_1_zero_flag), .out_5(n16_bit_alu_1_out_5));
  and and_1 (and_1_out, n16_bit_alu_1_zero_flag, control_signal_1_branch);
  RAM #(.addrWidth(16), .dataWidth(16), .bus("separate")) ram_2 (
    .addr(n16_bit_alu_1_out_5), .din(regfile_1_read_2_data), .data(ram_2_data), .str(control_signal_1_store),
    .sel(control_signal_1_data_memory_select), .clk(Clock), .ld(control_signal_1_load));  // open: clr
endmodule

module Chiron___FINAL_CPU (
  input  Clock
);

  wire and_1_out, control_signal_1_branch, control_signal_1_data_memory_select,
       control_signal_1_intermediate, control_signal_1_jump, control_signal_1_load,
       control_signal_1_regwrite, control_signal_1_store, n16_bit_alu_1_zero_flag, or_1_out;
  wire [2:0] control_signal_1_alu;
  wire [3:0] multiplexer_4_out, multiplexer_6_out, ram_1_data;
  wire [11:4] ram_1_data_2;
  wire [15:0] bit_extender_1_out, bit_extender_2_out, multiplexer_1_out, multiplexer_2_out,
       multiplexer_3_out, multiplexer_5_out, multiplexer_7_out, multiplexer_8_out, n16_bit_alu_1_out_5,
       n16_bit_carry_look_ahead_1_out_5, n16_bit_carry_look_ahead_2_out_5, ram_2_data, regfile_1_read_1_data,
       regfile_1_read_2_data, register_1_q;
  wire [20:12] ram_1_data_3;

  assign bit_extender_1_out = {{12{ram_1_data[3]}}, ram_1_data};  // Bit_Extender bit_extender_1
  Multiplexer #(.width(16), .enable("false")) multiplexer_1 (
    .in0(n16_bit_carry_look_ahead_2_out_5), .in1(n16_bit_carry_look_ahead_1_out_5), .out(multiplexer_1_out),
    .sel(and_1_out));
  _16_bit_carry_look_ahead u_16_bit_carry_look_ahead_1 (
    .A(n16_bit_carry_look_ahead_2_out_5), .B(bit_extender_1_out), .c_in(1'b0),
    .out_5(n16_bit_carry_look_ahead_1_out_5));  // open: Cout
  Register #(.width(16)) register_1 (.D(multiplexer_2_out), .Q(register_1_q), .clk(Clock));  // open: en, clr
  Multiplexer #(.width(16), .enable("false")) multiplexer_2 (
    .in0(multiplexer_1_out), .in1(multiplexer_3_out), .out(multiplexer_2_out), .sel(control_signal_1_jump));
  Multiplexer #(.width(16), .enable("false")) multiplexer_3 (
    .in0({register_1_q[15:12], ram_1_data_2, ram_1_data}), .in1(regfile_1_read_1_data),
    .out(multiplexer_3_out), .sel(control_signal_1_intermediate));
  _16_bit_carry_look_ahead u_16_bit_carry_look_ahead_2 (
    .A(16'h1), .B(register_1_q), .c_in(1'b0), .out_5(n16_bit_carry_look_ahead_2_out_5));  // open: Cout
  RAM #(.addrWidth(16), .dataWidth(21)) ram_1 (
    .addr(register_1_q), .data({ram_1_data_3, ram_1_data_2, ram_1_data}), .clk(Clock));  // open: sel, ld, clr
  Control_Signal control_signal_1 (
    .in_1(ram_1_data_3), .Intermediate(control_signal_1_intermediate), .RegWrite(control_signal_1_regwrite),
    .load(control_signal_1_load), .store(control_signal_1_store), .Branch(control_signal_1_branch),
    .Jump(control_signal_1_jump), .ALU(control_signal_1_alu),
    .Data_memory_Select(control_signal_1_data_memory_select));
  or or_1 (or_1_out, control_signal_1_branch, control_signal_1_store);
  Multiplexer #(.width(4), .enable("false")) multiplexer_4 (
    .in0(ram_1_data_2[11:8]), .in1(4'b1110), .out(multiplexer_4_out), .sel(control_signal_1_jump));
  Multiplexer #(.width(16), .enable("false")) multiplexer_5 (
    .in0(multiplexer_8_out), .in1(n16_bit_carry_look_ahead_2_out_5), .out(multiplexer_5_out),
    .sel(control_signal_1_jump));
  Multiplexer #(.width(4), .enable("false")) multiplexer_6 (
    .in0(ram_1_data), .in1(ram_1_data_2[11:8]), .out(multiplexer_6_out), .sel(or_1_out));
  REGFILE regfile_1 (
    .data_in(multiplexer_5_out), .Clock(Clock), .Write_Enable(control_signal_1_regwrite),
    .Write_Addr(multiplexer_4_out), .Read_Addr_1(ram_1_data_2[7:4]), .Read_Addr_2(multiplexer_6_out),
    .Read_1_Data(regfile_1_read_1_data), .Read_2_Data(regfile_1_read_2_data));
  assign bit_extender_2_out = {{12{ram_1_data[3]}}, ram_1_data};  // Bit_Extender bit_extender_2
  Multiplexer #(.width(16), .enable("false")) multiplexer_7 (
    .in0(regfile_1_read_2_data), .in1(bit_extender_2_out), .out(multiplexer_7_out),
    .sel(control_signal_1_intermediate));
  Multiplexer #(.width(16), .enable("false")) multiplexer_8 (
    .in0(n16_bit_alu_1_out_5), .in1(ram_2_data), .out(multiplexer_8_out), .sel(control_signal_1_load));
  _16_bit_ALU u_16_bit_alu_1 (
    .A(regfile_1_read_1_data), .B(multiplexer_7_out), .in_3(control_signal_1_alu),
    .Zero_Flag(n16_bit_alu_1_zero_flag), .out_5(n16_bit_alu_1_out_5));
  and and_1 (and_1_out, n16_bit_alu_1_zero_flag, control_signal_1_branch);
  RAM #(.addrWidth(16), .dataWidth(16), .bus("separate")) ram_2 (
    .addr(n16_bit_alu_1_out_5), .din(regfile_1_read_2_data), .data(ram_2_data), .str(control_signal_1_store),
    .sel(control_signal_1_data_memory_select), .clk(Clock), .ld(control_signal_1_load));  // open: clr

  // Notes on the sheet:
  //   Instruction mem
  //   opcode
  //   control unit
  //   src2
  //   dest
  //   src1
  //   jump
  //   write enable
  //   regfile
  //   imm
  //   load
  //   ALU
  //   branch
  //   ram mem
  //   store
endmodule

module _16_bit_ALU (
  input  [15:0] A,
  input  [15:0] B,
  input  [2:0] in_3,
  output Zero_Flag,
  output [15:0] out_5
);

  wire and_1_out, comparator_1_lt;
  wire [3:0] bit_extender_1_out, bit_extender_2_out;
  wire [15:0] and_2_out, bit_extender_3_out, multiplexer_1_out, n16_bit_carry_look_ahead_1_out_5, not_1_out,
       or_1_out, shifter_1_out, shifter_2_out;

  Multiplexer #(.width(16), .enable("false")) multiplexer_1 (
    .in0(B), .in1(not_1_out), .out(multiplexer_1_out), .sel(and_1_out));
  assign not_1_out = ~B;  // NOT_Gate not_1, 16 bits wide
  Bit_Extender #(.in_width(16), .out_width(4)) bit_extender_1 (.in(multiplexer_1_out), .out(bit_extender_1_out));
  Bit_Extender #(.in_width(16), .out_width(4)) bit_extender_2 (.in(multiplexer_1_out), .out(bit_extender_2_out));
  and and_1 (and_1_out, in_3[0], in_3[1]);
  _16_bit_carry_look_ahead u_16_bit_carry_look_ahead_1 (
    .A(A), .B(multiplexer_1_out), .c_in(and_1_out), .out_5(n16_bit_carry_look_ahead_1_out_5));  // open: Cout
  assign and_2_out = A & multiplexer_1_out;  // AND_Gate and_2, 16 bits wide
  assign or_1_out = A | multiplexer_1_out;  // OR_Gate or_1, 16 bits wide
  Shifter #(.width(16)) shifter_1 (.in(A), .\dist (bit_extender_1_out), .out(shifter_1_out));
  Shifter #(.width(16), .shift("lr")) shifter_2 (.in(A), .\dist (bit_extender_2_out), .out(shifter_2_out));
  Comparator #(.width(16)) comparator_1 (.a(A), .b(multiplexer_1_out), .lt(comparator_1_lt));  // open: gt, eq
  assign bit_extender_3_out = {{15{1'b0}}, comparator_1_lt};  // Bit_Extender bit_extender_3
  Multiplexer #(.select(3), .width(16), .enable("false")) multiplexer_2 (
    .in0(n16_bit_carry_look_ahead_1_out_5), .in1(and_2_out), .in2(or_1_out),
    .in3(n16_bit_carry_look_ahead_1_out_5), .in4(shifter_1_out), .in5(shifter_2_out),
    .in6(bit_extender_3_out), .in7(n16_bit_carry_look_ahead_1_out_5), .out(out_5), .sel(in_3));
  nor nor_1 (Zero_Flag, out_5[0], out_5[1], out_5[2], out_5[3], out_5[4], out_5[5], out_5[6], out_5[7], out_5[8], out_5[9], out_5[10], out_5[11], out_5[12], out_5[13], out_5[14], out_5[15]);
endmodule
